# Fritzing sketch two_relays_one_switch (saved by Fritzing 0.9.6b)
perfboards: 1

parts:
  OMRON1 = OMRON PCB Power Relay – G5LE [part_number="G5LE-1\n" package=THT]
  J2 = Screw terminal - 2 pins [package=THT]
  J3 = Screw terminal - 2 pins [package=THT]
  HLK-PM1 = HLK-PM01
  OMRON2 = OMRON PCB Power Relay – G5LE [part_number="G5LE-1\n" package=THT]
  S2 = SPST Switch [package=switch-spdt_kit]

nets:
  N1: OMRON1.COIL1, OMRON2.COIL1, S2.P
  N2: OMRON1.C, J2.pin2
  N3: OMRON1.B, HLK-PM1.AC#1, OMRON2.B
  N4: J2.pin1, J3.pin1, HLK-PM1.AC#0
  N5: J3.pin2, OMRON2.C
  N6: HLK-PM1.-Vo, S2.S
  N7: HLK-PM1.+Vo, OMRON2.COIL2

notes:
  AC GRID
